# Fritzing sketch arduino car (saved by Fritzing 0.9.9b)

parts:
  Bauteil1 = Arduino Mega 2560 (Rev3)
  L298N1 = L298N DC motor driver
  M1 = gear-motor
  M2 = gear-motor
  M3 = gear-motor
  M4 = gear-motor
  Bauteil2 = KY-033 Tracing Black White Line Hunting Sensor Module For Arduino
  Bauteil3 = KY-033 Tracing Black White Line Hunting Sensor Module For Arduino
  Bauteil4 = KY-033 Tracing Black White Line Hunting Sensor Module For Arduino
  HC-SR04_Sensor_1 = HC-SR04 Ultrasonic Distance Sensor
  HC-SR04_Sensor_2 = HC-SR04 Ultrasonic Distance Sensor

nets:
  VIN: Bauteil1.VIN, L298N1.5V
  N1: Bauteil1.D2_PWM, L298N1.ENA
  N2: Bauteil1.D3_PWM, L298N1.IN1
  N3: Bauteil1.D4_PWM, L298N1.IN2
  N4: Bauteil1.D5_PWM, L298N1.IN3
  N5: Bauteil1.D6_PWM, L298N1.IN4
  N6: Bauteil1.D7_PWM, L298N1.ENB
  N7: Bauteil1.D24, HC-SR04_Sensor_1.TRIG
  N8: Bauteil1.D25, HC-SR04_Sensor_1.ECHO
  N9: Bauteil1.D26, HC-SR04_Sensor_2.TRIG
  N10: Bauteil1.D27, HC-SR04_Sensor_2.ECHO
  N11: Bauteil1.D30, Bauteil2.S
  N12: Bauteil1.D32, Bauteil4.S
  N13: Bauteil1.D34, Bauteil3.S
  N14: L298N1.OUT1, M1.pin_2, M2.pin_2
  N15: L298N1.OUT2, M1.pin_1, M2.pin_1
  N16: L298N1.OUT3, M3.pin_1, M4.pin_1
  N17: L298N1.OUT4, M3.pin_2, M4.pin_2

notes:
  12 V Power Source
  Left DC Motors
  Right DC Motors

custom parts:
  L298N DC motor driver: 2x DC motor driver with 78M05 positive voltage regulator (7..35 V) L298N: max 46 V, 2 A Set 5 V Enable jumper to enable 5 V regultor (needed for the L298N) and +5 V output at screw terminal or supply external +5 V at screw terminal Set ENA and/or ENB to +5 V to enable motor permanently or supply ENA and/or ENB with PWM signal IN1 and IN2 set rotation directory for motor A (OUT1/OUT2) IN2 and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
  KY-033 Tracing Black White Line Hunting Sensor Module For Arduino: Tracing Black White Line Hunting Sensor Module For Arduino Description: This is KY-033 tracking sensor. The KY-033 measures the intensity of infrared radiation and delivers it as an analog output voltage. Features: Operating voltage: 2.5 - 12V(cannot over12V) working current: 18mA-20mA at 5V Enhanced accuracy Documents: http://www.vishay.com/docs/83760/tcrt5000.pdf
